// Logisim project ULA 5 BITS 2.0.circ as structural Verilog
module main (
  input  S0,
  input  S1,
  input  S2,
  input  A0,
  input  A1,
  input  A2,
  input  A3,
  input  A4,
  input  B0,
  input  B1,
  input  B2,
  input  B3,
  input  B4,
  output out_14,
  output out_15,
  output out_16,
  output out_17,
  output out_18,
  output out_19,
  output out_20,
  output out_21,
  output out_22,
  output out_23,
  output out_24,
  output out_25,
  output out_26,
  output out_27,
  output out_28,
  output out_29,
  output out_30
);

  wire _2A_out_11, _2A_out_12, _2A_out_13, _2A_out_14, _2A_out_15;
  wire [4:0] adder_1_out, subtractor_1_out;

  AND_5_BITS AND (
    .in_1(A0), .in_2(A1), .in_3(A2), .in_4(A3), .in_5(A4), .in_6(B0), .in_7(B1), .in_8(B2), .in_9(B3),
    .in_10(B4), .out_11(out_16), .out_12(out_17), .out_13(out_18), .out_14(out_19), .out_15(out_20));
  OR_5_BITS OR (
    .in_1(A0), .in_2(A1), .in_3(A2), .in_4(A3), .in_5(A4), .in_6(B0), .in_7(B1), .in_8(B2), .in_9(B3),
    .in_10(B4), .out_11(out_21), .out_12(out_22), .out_13(out_23), .out_14(out_24), .out_15(out_25));
  AND_5_BITS _2A (
    .in_1(A0), .in_2(A1), .in_3(A2), .in_4(A3), .in_5(A4), .in_6(A0), .in_7(A1), .in_8(A2), .in_9(A3),
    .in_10(A4), .out_11(_2A_out_11), .out_12(_2A_out_12), .out_13(_2A_out_13), .out_14(_2A_out_14),
    .out_15(_2A_out_15));
  INVERSOR_5_BITS NOT_A (
    .in_1(A0), .in_2(A1), .in_3(A2), .in_4(A3), .in_5(A4), .out_6(out_26), .out_7(out_27), .out_8(out_28),
    .out_9(out_29), .out_10(out_30));
  Adder #(.width(5)) adder_1 (
    .a({A4, A3, A2, A1, A0}), .b({B4, B3, B2, B1, B0}), .out(adder_1_out), .cin(1'b0), .cout(out_14));
  Subtractor #(.width(5)) subtractor_1 (
    .a({A4, A3, A2, A1, A0}), .b({B4, B3, B2, B1, B0}), .out(subtractor_1_out), .bin(1'b0), .bout(out_15));
endmodule

module OR_5_BITS (
  input  in_1,
  input  in_2,
  input  in_3,
  input  in_4,
  input  in_5,
  input  in_6,
  input  in_7,
  input  in_8,
  input  in_9,
  input  in_10,
  output out_11,
  output out_12,
  output out_13,
  output out_14,
  output out_15
);

  or or_1 (out_11, in_1, in_6);
  or or_2 (out_12, in_2, in_7);
  or or_3 (out_13, in_3, in_8);
  or or_4 (out_14, in_4, in_9);
  or or_5 (out_15, in_5, in_10);
endmodule

module AND_5_BITS (
  input  in_1,
  input  in_2,
  input  in_3,
  input  in_4,
  input  in_5,
  input  in_6,
  input  in_7,
  input  in_8,
  input  in_9,
  input  in_10,
  output out_11,
  output out_12,
  output out_13,
  output out_14,
  output out_15
);

  and and_1 (out_11, in_1, in_6);
  and and_2 (out_12, in_2, in_7);
  and and_3 (out_13, in_3, in_8);
  and and_4 (out_14, in_4, in_9);
  and and_5 (out_15, in_5, in_10);
endmodule

module COMPARADOR_1_BIT (
  input  A,
  input  B,
  output IGUAL,
  output B_A,
  output A_B
);

  wire not_1_out, not_2_out;

  not not_1 (not_1_out, B);
  not not_2 (not_2_out, A);
  xnor xnor_1 (IGUAL, A, B);
  and and_1 (B_A, A, not_1_out);
  and and_2 (A_B, not_2_out, B);
endmodule

module DISPLAY_7X2_SEGMENTOS (
  input  A,
  input  B,
  input  C,
  input  D,
  input  E,
  output out_6,
  output out_7,
  output out_8,
  output out_9,
  output out_10,
  output out_11,
  output out_12,
  output out_13,
  output out_14
);

  wire and_1_out, and_2_out, and_3_out, and_4_out, and_5_out, and_6_out, and_7_out, and_8_out, and_9_out,
       and_10_out, and_11_out, and_12_out, and_13_out, and_14_out, and_15_out, and_16_out, and_17_out,
       and_18_out, and_19_out, and_20_out, and_21_out, and_22_out, and_23_out, and_24_out, and_25_out,
       and_26_out, and_27_out, and_28_out, and_29_out, and_30_out, and_31_out, and_32_out, and_33_out,
       and_34_out, and_35_out, and_36_out, not_1_out, not_2_out, not_3_out, not_4_out, not_5_out;

  not not_1 (not_1_out, A);
  not not_2 (not_2_out, B);
  not not_3 (not_3_out, C);
  not not_4 (not_4_out, D);
  not not_5 (not_5_out, E);
  and and_1 (and_1_out, not_1_out, not_2_out);
  and and_2 (and_2_out, not_2_out, C);
  and and_3 (and_3_out, A, B);
  and and_4 (and_4_out, not_1_out, not_3_out, not_4_out);
  and and_5 (and_5_out, not_2_out, not_3_out);
  and and_6 (and_6_out, B, C, D);
  and and_7 (and_7_out, not_1_out, not_2_out);
  and and_8 (and_8_out, not_2_out, C);
  and and_9 (and_9_out, A, B);
  and and_10 (and_10_out, not_1_out, not_2_out, not_3_out);
  and and_11 (and_11_out, not_1_out, not_2_out);
  and and_12 (and_12_out, not_2_out, C);
  and and_13 (and_13_out, not_1_out, not_3_out, not_4_out);
  and and_14 (and_14_out, A, C, not_4_out);
  and and_15 (and_15_out, A, B, not_3_out);
  and and_16 (and_16_out, not_2_out, D);
  and and_17 (and_17_out, not_1_out, not_3_out, not_5_out);
  and and_18 (and_18_out, not_1_out, C, E);
  and and_19 (and_19_out, not_1_out, B, not_4_out);
  and and_20 (and_20_out, B, C, not_4_out);
  and and_21 (and_21_out, A, not_2_out, not_5_out);
  and and_22 (and_22_out, A, not_3_out, E);
  and and_23 (and_23_out, A, D, not_5_out);
  and and_24 (and_24_out, A, C);
  and and_25 (and_25_out, not_1_out, not_4_out, not_5_out);
  and and_26 (and_26_out, not_2_out, not_3_out, E);
  and and_27 (and_27_out, not_2_out, not_3_out, D);
  and and_28 (and_28_out, not_2_out, D, E);
  and and_29 (and_29_out, not_3_out, D, E);
  and and_30 (and_30_out, not_1_out, B, not_4_out);
  and and_31 (and_31_out, not_1_out, B, not_5_out);
  and and_32 (and_32_out, B, D, not_5_out);
  or or_1 (out_6, and_1_out, and_2_out, and_3_out, and_4_out);
  or or_2 (out_8, and_5_out, not_1_out, and_6_out);
  or or_3 (out_9, and_7_out, and_8_out, and_9_out, and_10_out);
  and and_33 (and_33_out, not_1_out, not_2_out);
  or or_4 (out_11, and_33_out, and_34_out);
  and and_34 (and_34_out, not_1_out, not_3_out, not_4_out);
  and and_35 (and_35_out, A, C);
  or or_5 (out_12, and_35_out, and_36_out);
  and and_36 (and_36_out, A, B);
  or or_6 (out_10, and_11_out, and_12_out, and_13_out, and_14_out, and_15_out);
  or or_7 (out_13, and_16_out, and_17_out, and_18_out, and_19_out, and_20_out, and_21_out, and_22_out, and_23_out);
  or or_8 (out_14, and_24_out, and_25_out, and_26_out, and_27_out, and_28_out, and_29_out, and_30_out, and_31_out, and_32_out);

  assign out_7 = 1'b1;
endmodule

module INVERSOR_5_BITS (
  input  in_1,
  input  in_2,
  input  in_3,
  input  in_4,
  input  in_5,
  output out_6,
  output out_7,
  output out_8,
  output out_9,
  output out_10
);

  not not_1 (out_6, in_1);
  not not_2 (out_7, in_2);
  not not_3 (out_8, in_3);
  not not_4 (out_9, in_4);
  not not_5 (out_10, in_5);
endmodule
